# Fritzing sketch Untitled Sketch 2 (saved by Fritzing 0.9.3b)

parts:
  Part1 = Arduino Uno (Rev3)
  A1 = DM860A Stepper Motor Driver
  M1 = Stepper Motor - Bipolar
  S1 = Round Pushbutton
  A2 = DM860A Stepper Motor Driver
  M2 = Stepper Motor - Bipolar
  Power_plug1 = Power plug
  VCC1 = Battery block 9V

nets:
  GND: Part1.GND, A1.GND, A1.ENBL-(ENB), A1.DIR-(DIR), A1.PUL-(PUL), S1.leg0, A2.GND, A2.ENBL-(ENB), A2.DIR-(DIR), A2.PUL-(PUL), Power_plug1.GND, VCC1.+
  N1: Part1.D1/TX, A1.PUL+(+5V)
  N2: Part1.D2, A1.DIR+(+5V)
  N3: Part1.D3_PWM, A1.ENBL+(+5V)
  N4: Part1.D4, A2.PUL+(+5V)
  N5: Part1.D5_PWM, A2.DIR+(+5V)
  N6: Part1.D6_PWM, A2.ENBL+(+5V)
  N7: Part1.5V, VCC1.-
  N8: A1.B-, M1.D
  N9: A1.B+, M1.B
  N10: A1.A-, M1.C
  N11: A1.A+, M1.A
  N12: A1.VDC, S1.leg1, A2.VDC, Power_plug1.VCC
  N13: A2.B-, M2.D
  N14: A2.B+, M2.B
  N15: A2.A-, M2.C
  N16: A2.A+, M2.A

custom parts:
  DM860A Stepper Motor Driver: DM860A is a type of two-phase hybrid stepping motor driver, The drive voltage of which is from 24VDC to 80VDC. It is designed for use with 2-phase hybrid stepper motor of all kinds with 57mm to 110mm outside diameter and less than 8.0A phase current. Mar 2023: Correct pcb layerId as the part won't save correctly in a .fzz file as is.
